// Logisim project Lab-4-Given.circ as structural Verilog: 17 circuits, main circuit Main
module Main (
);

  wire ALUOp0, ALUOp1, ALUSrcB, and_1_out, and_2_out, and_3_out, and_4_out, Branch, CLK, FwdJR, FwdRegA,
       FwdRegB, JAL, MemRead, MemToReg, MemWrite, or_1_out, PCSource0, PCSource1, RegDst, RegWrite, Squash,
       Zero1, Zero2;
  wire [1:0] FwdA, FwdB;
  wire [3:0] ALUCtl0, ALUCtl1, ALUCtl2, ALUCtl3;
  wire [4:0] WrAddr, WrAddr1, WrAddr2, WrAddr3;
  wire [5:0] Func;
  wire [10:3] Signals2;
  wire [11:0] Signals0, Signals1, Signals3;
  wire [31:0] adder_1_out, adder_2_out, adder_4_out, alu_1_aluresult, ALUout2, ALUout3, bit_extender_1_out,
       BranchPC1, BranchPC2, FwdData3, ID_EX_rddata2_2, Instr1, Instr2, Instr3, multiplexer_1_out,
       multiplexer_4_out, multiplexer_5_out, multiplexer_9_out, multiplexer_10_out, multiplexer_11_out,
       multiplexer_12_out, Offset1, PC, PC0, PC1, PC2, PC3, PCin, ram_1_data, ReadData2, ReadData3,
       register_file_1_rddata1, register_file_1_rddata2, RSAddr1, RSAddr2, WrData3, WriteData1, WriteData2;
  wire [31:6] Instr0;

  Register #(.width(32)) u_PC (.D(PCin), .Q(PC), .clk(CLK));  // open: en, clr
  Clock clock_1 (.out(CLK));
  Ctl ctl_1 (.Op(Instr0[31:26]), .Func(Func), .Signals(Signals0), .ALUCtl(ALUCtl0));
  RAM #(.dataWidth(32)) ram_1 (.addr(PC[9:2]), .data(ram_1_data), .clk(CLK));  // open: sel, ld, clr
  IF_ID IF_ID (
    .PCP4(PC), .Instruction(ram_1_data), .Squash(Squash), .CLK(CLK), .PCP4_2(PC0),
    .Instruction_2({Instr0, Func}));
  Multiplexer #(.width(32), .enable("false")) multiplexer_1 (
    .in0(ALUout3), .in1(ReadData3), .out(multiplexer_1_out), .sel(MemToReg));
  Adder #(.width(32)) adder_1 (.a(32'h4), .b(PC2), .out(adder_1_out));  // open: cin, cout
  Multiplexer #(.width(5), .enable("false")) multiplexer_2 (.in0(WrAddr3), .in1({5{1'b1}}), .out(WrAddr), .sel(JAL));
  // Probe on WrAddr
  or or_1 (or_1_out, RegWrite, JAL);
  Multiplexer #(.width(32), .enable("false")) multiplexer_3 (
    .in0(multiplexer_1_out), .in1(adder_1_out), .out(WrData3), .sel(JAL));
  // Probe on WrData3
  // Probe on Instr0[25:21]
  // Probe on Instr0[20:16]
  Register_File register_file_1 (
    .WrAddr(WrAddr), .WrData(WrData3), .WrReg(or_1_out), .RdAddr1(Instr0[25:21]), .RdAddr2(Instr0[20:16]),
    .RdData1(register_file_1_rddata1), .RdData2(register_file_1_rddata2), .Clock(CLK));
  Multiplexer #(.width(32), .enable("false")) multiplexer_4 (
    .in0(register_file_1_rddata1), .in1(WrData3), .out(multiplexer_4_out), .sel(FwdRegA));
  Multiplexer #(.width(32), .enable("false")) multiplexer_5 (
    .in0(register_file_1_rddata2), .in1(WrData3), .out(multiplexer_5_out), .sel(FwdRegB));
  Multiplexer #(.select(2), .width(5), .enable("false")) multiplexer_6 (
    .in0(Instr1[20:16]), .in1(Instr1[15:11]), .in2({5{1'b1}}), .in3({5{1'b1}}), .out(WrAddr1),
    .sel({JAL, RegDst}));
  ID_EX ID_EX (
    .PCP4(PC0), .RdData1(multiplexer_4_out), .RdData2(multiplexer_5_out), .Instruction({Instr0, Func}),
    .Signals(Signals0), .ALUCtl(ALUCtl0), .Squash(Squash), .CLK(CLK), .PCP4_2(PC1), .RdData1_2(RSAddr1),
    .RdData2_2(ID_EX_rddata2_2), .Instruction_2(Instr1),
    .Signals_2({Signals1[11], RegDst, Signals1[9], ALUSrcB, ALUOp0, ALUOp1, Signals1[5:0]}),
    .ALUCtl_2(ALUCtl1));  // open: WrAddr, WrAddr_2
  Adder #(.width(32)) adder_2 (.a(32'h4), .b(PC1), .out(adder_2_out));  // open: cin, cout
  Adder #(.width(32)) adder_3 (.a(adder_2_out), .b(Offset1), .out(BranchPC1));  // open: cin, cout
  and and_1 (and_1_out, PCSource1, PCSource0);
  Register_Forwarding_Unit register_forwarding_unit_1 (
    .RAddrA(Instr0[25:21]), .RAddrB(Instr0[20:16]), .WrAddr(WrAddr), .RegWrite(RegWrite), .FwdA(FwdRegA),
    .FwdB(FwdRegB));
  JR_Forwarding_Unit jr_forwarding_unit_1 (
    .JR(and_1_out), .WrAddr(WrAddr), .RAddrJR(Instr2[25:21]), .RegWrite(RegWrite), .FwdJR(FwdJR));
  Multiplexer #(.select(2), .width(32), .enable("false")) multiplexer_7 (
    .in0(ID_EX_rddata2_2), .in1(FwdData3), .in2(ALUout2), .in3(ReadData2), .out(WriteData1), .sel(FwdB));
  Multiplexer #(.width(32), .enable("false")) multiplexer_8 (
    .in0(ALUout3), .in1(ReadData3), .out(FwdData3), .sel(Signals3[1]));
  assign bit_extender_1_out = {{16{Instr1[15]}}, Instr1[15:0]};  // Bit_Extender bit_extender_1
  Multiplexer #(.select(2), .width(32), .enable("false")) multiplexer_9 (
    .in0(RSAddr1), .in1(FwdData3), .in2(ALUout2), .in3(ReadData2), .out(multiplexer_9_out), .sel(FwdA));
  Multiplexer #(.width(32), .enable("false")) multiplexer_10 (
    .in0(WriteData1), .in1(bit_extender_1_out), .out(multiplexer_10_out), .sel(ALUSrcB));
  Shifter #(.width(32)) shifter_1 (.in(bit_extender_1_out), .\dist (5'b00010), .out(Offset1));
  Forwarding_Unit forwarding_unit_1 (
    .RAddrA(Instr1[25:21]), .RAddrB(Instr1[20:16]), .WrAddrEM(WrAddr2), .WrAddrMW(WrAddr3),
    .SignalEM({JAL, Signals2[10:6], PCSource0, PCSource1, Signals2[3], MemWrite, MemRead, Branch}),
    .SignalMW({Signals3[11:10], RegWrite, Signals3[8:4], MemToReg, Signals3[2:0]}), .FwdA(FwdA), .FwdB(FwdB));
  ALU alu_1 (
    .ALUCtl(ALUCtl1), .A(multiplexer_9_out), .B(multiplexer_10_out), .ALUResult(alu_1_aluresult),
    .Zero(Zero1), .Shamt(Instr1[10:6]));  // open: Overflow
  Adder #(.width(32)) adder_4 (.a(32'h4), .b(PC), .out(adder_4_out));  // open: cin, cout
  Multiplexer #(.width(32), .enable("false")) multiplexer_11 (
    .in0(RSAddr2), .in1(WrData3), .out(multiplexer_11_out), .sel(FwdJR));
  Multiplexer #(.select(2), .width(32), .enable("false")) multiplexer_12 (
    .in0(adder_4_out), .in1(adder_4_out), .in2({PC2[31:28], Instr2[25:0], 2'b00}), .in3(multiplexer_11_out),
    .out(multiplexer_12_out), .sel({PCSource1, PCSource0}));
  Multiplexer #(.width(32), .enable("false")) multiplexer_13 (
    .in0(multiplexer_12_out), .in1(BranchPC2), .out(PCin), .sel(and_2_out));
  and and_2 (and_2_out, Branch, Zero2);
  EX_MEM ex_mem_1 (
    .PCP4(PC1), .JumpPC(BranchPC1), .ALUOut(alu_1_aluresult), .WriteData(WriteData1), .Instruction(Instr1),
    .RSAddr(RSAddr1), .Signal({Signals1[11], RegDst, Signals1[9], ALUSrcB, ALUOp0, ALUOp1, Signals1[5:0]}),
    .ALUCtl(ALUCtl1), .Zero(Zero1), .WrAddr(WrAddr1), .CLK(CLK), .PCP4_2(PC2), .JumpPC_2(BranchPC2),
    .ALUOut_2(ALUout2), .WriteData_2(WriteData2), .Instruction_2(Instr2), .RSAddr_2(RSAddr2),
    .Signal_2({JAL, Signals2[10:6], PCSource0, PCSource1, Signals2[3], MemWrite, MemRead, Branch}),
    .ALUCtl_2(ALUCtl2), .Zero_2(Zero2), .WrAddr_2(WrAddr2));  // open: Squash
  and and_3 (and_3_out, PCSource1, ~PCSource0);  // AND_Gate
  RAM #(.dataWidth(32), .bus("separate")) ram_2 (
    .addr(ALUout2[7:0]), .din(WriteData2), .data(ReadData2), .str(MemWrite), .clk(CLK), .ld(MemRead));  // open: sel, clr
  and and_4 (and_4_out, PCSource1, PCSource0);
  or or_2 (Squash, and_3_out, and_2_out, and_4_out);
  MEM_WB mem_wb_1 (
    .PC(PC2), .ReadData(ReadData2), .ALUOut(ALUout2), .Instruction(Instr2), .WrAddr(WrAddr2),
    .Signal({JAL, Signals2[10:6], PCSource0, PCSource1, Signals2[3], MemWrite, MemRead, Branch}),
    .ALUCtl(ALUCtl2), .CLK(CLK), .PC_2(PC3), .ReadData_2(ReadData3), .ALUOut_2(ALUout3),
    .Instruction_2(Instr3), .WrAddr_2(WrAddr3),
    .Signal_2({Signals3[11:10], RegWrite, Signals3[8:4], MemToReg, Signals3[2:0]}), .ALUCtl_2(ALUCtl3));

  // Other names for the same wires on the sheet: Signals1 (some bits) = {RegDst, ALUSrcB, ALUOp0, ALUOp1};
  //   Signals2 (some bits) = {JAL, PCSource0, PCSource1, MemWrite, MemRead, Branch}; Instr0[5:0] = Func;
  //   Instr0_16[15:0] = {Instr0[15:6], Func}; RDAddr2[4:0] = Instr0[20:16]; Opcode[5:0] = Instr0[31:26];
  //   Signals3 (some bits) = {RegWrite, MemToReg}

  // Notes on the sheet:
  //   JR
  //   Jump
endmodule

module _32_Bit_Adder___Subtractor (
  input  Add_Sub_control,
  input  [31:0] in_2,
  input  [31:0] in_3,
  output [31:0] out_4,
  output carry_out
);

  wire adder_1_cout, subtractor_1_bout;
  wire [31:0] adder_1_out, subtractor_1_out;

  Adder #(.width(32)) adder_1 (.a(in_2), .b(in_3), .out(adder_1_out), .cout(adder_1_cout));  // open: cin
  Subtractor #(.width(32)) subtractor_1 (
    .a(in_2), .b(in_3), .out(subtractor_1_out), .bout(subtractor_1_bout));  // open: bin
  Multiplexer #(.width(32), .enable("false")) multiplexer_1 (
    .in0(adder_1_out), .in1(subtractor_1_out), .out(out_4), .sel(Add_Sub_control));
  Multiplexer #(.enable("false")) multiplexer_2 (
    .in0(adder_1_cout), .in1(subtractor_1_bout), .out(carry_out), .sel(Add_Sub_control));
endmodule

module ALU (
  input  [3:0] ALUCtl,
  input  [31:0] A,
  input  [31:0] B,
  input  [4:0] Shamt,
  output [31:0] ALUResult,
  output Zero,
  output Overflow
);

  wire comparator_1_lt, comparator_2_lt, comparator_3_eq, comparator_4_eq, or_2_out;
  wire [31:0] Add, And, LessThan, LessThanUnsigned, Nor, Or, ShiftLeft, ShiftRight, Sub, Xor;

  // Probe on ALUCtl
  assign Nor = ~(A | B);  // NOR_Gate nor_1, 32 bits wide
  Adder #(.width(32)) adder_1 (.a(A), .b(B), .out(Add));  // open: cin, cout
  Subtractor #(.width(32)) subtractor_1 (.a(A), .b(B), .out(Sub));  // open: bin, bout
  assign And = A & B;  // AND_Gate and_1, 32 bits wide
  assign Or = A | B;  // OR_Gate or_1, 32 bits wide
  assign Xor = A ^ B;  // XOR_Gate xor_1, 32 bits wide
  Comparator #(.width(32)) comparator_1 (.a(A), .b(B), .lt(comparator_1_lt));  // open: gt, eq
  assign LessThan = {{31{1'b0}}, comparator_1_lt};  // Bit_Extender bit_extender_1
  Shifter #(.width(32)) shifter_1 (.in(B), .\dist (Shamt), .out(ShiftLeft));
  Shifter #(.width(32), .shift("lr")) shifter_2 (.in(B), .\dist (Shamt), .out(ShiftRight));
  Comparator #(.width(32), .mode("unsigned")) comparator_2 (.a(A), .b(B), .lt(comparator_2_lt));  // open: gt, eq
  assign LessThanUnsigned = {{31{1'b0}}, comparator_2_lt};  // Bit_Extender bit_extender_2
  Multiplexer #(.select(4), .width(32), .enable("false")) multiplexer_1 (
    .in0(Or), .in1(LessThanUnsigned), .in2(LessThan), .in3(Add), .in4(Sub), .in5(Xor), .in6(And),
    .in14(ShiftRight), .in15(ShiftLeft), .out(ALUResult), .sel(ALUCtl));  // open: in7, in8, in9, in10, in11, in12, in13
  Comparator #(.width(4)) comparator_3 (.a(4'b0011), .b(ALUCtl), .eq(comparator_3_eq));  // open: gt, lt
  Comparator #(.width(4)) comparator_4 (.a(ALUCtl), .b(4'b0100), .eq(comparator_4_eq));  // open: gt, lt
  Overflow overflow_1 (
    .Add(comparator_3_eq), .Sub(comparator_4_eq), .ASign(A[31]), .BSign(B[31]), .ResultSign(ALUResult[31]),
    .Overflow(Overflow));
  not not_1 (Zero, or_2_out);
  or or_2 (or_2_out, ALUResult[0], ALUResult[1], ALUResult[2], ALUResult[3], ALUResult[4], ALUResult[5], ALUResult[6], ALUResult[7], ALUResult[8], ALUResult[9], ALUResult[10], ALUResult[11], ALUResult[12], ALUResult[13], ALUResult[14], ALUResult[15], ALUResult[16], ALUResult[17], ALUResult[18], ALUResult[19], ALUResult[20], ALUResult[21], ALUResult[22], ALUResult[23], ALUResult[24], ALUResult[25], ALUResult[26], ALUResult[27], ALUResult[28], ALUResult[29], ALUResult[30], ALUResult[31]);

  // Other names for the same wires on the sheet: ASign = A[31]; ResultSign = ALUResult[31]; BSign = B[31]
endmodule

module Register_File (
  input  [4:0] WrAddr,
  input  [31:0] WrData,
  input  WrReg,
  input  [4:0] RdAddr1,
  input  [4:0] RdAddr2,
  input  Clock,
  output [31:0] RdData1,
  output [31:0] RdData2
);

  wire WrReg0, WrReg1, WrReg2, WrReg3, WrReg4, WrReg5, WrReg6, WrReg7, WrReg8, WrReg9, WrReg10, WrReg11,
       WrReg12, WrReg13, WrReg14, WrReg15, WrReg16, WrReg17, WrReg18, WrReg19, WrReg20, WrReg21, WrReg22,
       WrReg23, WrReg24, WrReg25, WrReg26, WrReg27, WrReg28, WrReg29, WrReg30, WrReg31;
  wire [31:0] RegData1, RegData2, RegData3, RegData4, RegData5, RegData6, RegData7, RegData8, RegData9,
       RegData10, RegData11, RegData12, RegData13, RegData14, RegData15, RegData16, RegData17, RegData18,
       RegData19, RegData20, RegData21, RegData22, RegData23, RegData24, RegData25, RegData26, RegData27,
       RegData28, RegData29, RegData30, RegData31;

  Demultiplexer #(.select(5), .enable("false")) demultiplexer_1 (
    .out0(WrReg0), .out1(WrReg1), .out2(WrReg2), .out3(WrReg3), .out4(WrReg4), .out5(WrReg5), .out6(WrReg6),
    .out7(WrReg7), .out8(WrReg8), .out9(WrReg9), .out10(WrReg10), .out11(WrReg11), .out12(WrReg12),
    .out13(WrReg13), .out14(WrReg14), .out15(WrReg15), .out16(WrReg16), .out17(WrReg17), .out18(WrReg18),
    .out19(WrReg19), .out20(WrReg20), .out21(WrReg21), .out22(WrReg22), .out23(WrReg23), .out24(WrReg24),
    .out25(WrReg25), .out26(WrReg26), .out27(WrReg27), .out28(WrReg28), .out29(WrReg29), .out30(WrReg30),
    .out31(WrReg31), .in(WrReg), .sel(WrAddr));
  // Probe on RegData4
  Register #(.width(32)) Reg4 (.D(WrData), .en(WrReg4), .Q(RegData4), .clk(Clock));  // open: clr
  // Probe on RegData8
  Register #(.width(32)) Reg8 (.D(WrData), .en(WrReg8), .Q(RegData8), .clk(Clock));  // open: clr
  // Probe on RegData12
  Register #(.width(32)) Reg12 (.D(WrData), .en(WrReg12), .Q(RegData12), .clk(Clock));  // open: clr
  // Probe on RegData16
  Register #(.width(32)) Reg16 (.D(WrData), .en(WrReg16), .Q(RegData16), .clk(Clock));  // open: clr
  // Probe on RegData20
  Register #(.width(32)) Reg20 (.D(WrData), .en(WrReg20), .Q(RegData20), .clk(Clock));  // open: clr
  // Probe on RegData24
  Register #(.width(32)) Reg24 (.D(WrData), .en(WrReg24), .Q(RegData24), .clk(Clock));  // open: clr
  // Probe on RegData28
  Register #(.width(32)) Reg28 (.D(WrData), .en(WrReg28), .Q(RegData28), .clk(Clock));  // open: clr
  Register #(.width(32)) Reg1 (.D(WrData), .en(WrReg1), .Q(RegData1), .clk(Clock));  // open: clr
  Register #(.width(32)) Reg5 (.D(WrData), .en(WrReg5), .Q(RegData5), .clk(Clock));  // open: clr
  Register #(.width(32)) Reg9 (.D(WrData), .en(WrReg9), .Q(RegData9), .clk(Clock));  // open: clr
  Register #(.width(32)) Reg13 (.D(WrData), .en(WrReg13), .Q(RegData13), .clk(Clock));  // open: clr
  Register #(.width(32)) Reg17 (.D(WrData), .en(WrReg17), .Q(RegData17), .clk(Clock));  // open: clr
  Register #(.width(32)) Reg21 (.D(WrData), .en(WrReg21), .Q(RegData21), .clk(Clock));  // open: clr
  Register #(.width(32)) Reg25 (.D(WrData), .en(WrReg25), .Q(RegData25), .clk(Clock));  // open: clr
  Register #(.width(32)) Reg29 (.D(WrData), .en(WrReg29), .Q(RegData29), .clk(Clock));  // open: clr
  // Probe on RegData1
  // Probe on RegData5
  // Probe on RegData9
  // Probe on RegData13
  // Probe on RegData17
  // Probe on RegData21
  // Probe on RegData25
  // Probe on RegData29
  // Probe on RegData2
  Register #(.width(32)) Reg2 (.D(WrData), .en(WrReg2), .Q(RegData2), .clk(Clock));  // open: clr
  // Probe on RegData6
  Register #(.width(32)) Reg6 (.D(WrData), .en(WrReg6), .Q(RegData6), .clk(Clock));  // open: clr
  // Probe on RegData10
  Register #(.width(32)) Reg10 (.D(WrData), .en(WrReg10), .Q(RegData10), .clk(Clock));  // open: clr
  // Probe on RegData14
  Register #(.width(32)) Reg14 (.D(WrData), .en(WrReg14), .Q(RegData14), .clk(Clock));  // open: clr
  // Probe on RegData18
  Register #(.width(32)) Reg18 (.D(WrData), .en(WrReg18), .Q(RegData18), .clk(Clock));  // open: clr
  // Probe on RegData22
  Register #(.width(32)) Reg22 (.D(WrData), .en(WrReg22), .Q(RegData22), .clk(Clock));  // open: clr
  // Probe on RegData26
  Register #(.width(32)) Reg26 (.D(WrData), .en(WrReg26), .Q(RegData26), .clk(Clock));  // open: clr
  // Probe on RegData30
  Register #(.width(32)) Reg30 (.D(WrData), .en(WrReg30), .Q(RegData30), .clk(Clock));  // open: clr
  // Probe on RegData3
  Register #(.width(32)) Reg3 (.D(WrData), .en(WrReg3), .Q(RegData3), .clk(Clock));  // open: clr
  // Probe on RegData7
  Register #(.width(32)) Reg7 (.D(WrData), .en(WrReg7), .Q(RegData7), .clk(Clock));  // open: clr
  // Probe on RegData11
  Register #(.width(32)) Reg11 (.D(WrData), .en(WrReg11), .Q(RegData11), .clk(Clock));  // open: clr
  // Probe on RegData15
  Register #(.width(32)) Reg15 (.D(WrData), .en(WrReg15), .Q(RegData15), .clk(Clock));  // open: clr
  // Probe on RegData19
  Register #(.width(32)) Reg19 (.D(WrData), .en(WrReg19), .Q(RegData19), .clk(Clock));  // open: clr
  // Probe on RegData23
  Register #(.width(32)) Reg23 (.D(WrData), .en(WrReg23), .Q(RegData23), .clk(Clock));  // open: clr
  // Probe on RegData27
  Register #(.width(32)) Reg27 (.D(WrData), .en(WrReg27), .Q(RegData27), .clk(Clock));  // open: clr
  // Probe on RegData31
  Register #(.width(32)) Reg31 (.D(WrData), .en(WrReg31), .Q(RegData31), .clk(Clock));  // open: clr
  Multiplexer #(.select(5), .width(32), .enable("false")) multiplexer_1 (
    .in0({32{1'b0}}), .in1(RegData1), .in2(RegData2), .in3(RegData3), .in4(RegData4), .in5(RegData5),
    .in6(RegData6), .in7(RegData7), .in8(RegData8), .in9(RegData9), .in10(RegData10), .in11(RegData11),
    .in12(RegData12), .in13(RegData13), .in14(RegData14), .in15(RegData15), .in16(RegData16),
    .in17(RegData17), .in18(RegData18), .in19(RegData19), .in20(RegData20), .in21(RegData21),
    .in22(RegData22), .in23(RegData23), .in24(RegData24), .in25(RegData25), .in26(RegData26),
    .in27(RegData27), .in28(RegData28), .in29(RegData29), .in30(RegData30), .in31(RegData31), .out(RdData1),
    .sel(RdAddr1));
  Multiplexer #(.select(5), .width(32), .enable("false")) multiplexer_2 (
    .in0({32{1'b0}}), .in1(RegData1), .in2(RegData2), .in3(RegData3), .in4(RegData4), .in5(RegData5),
    .in6(RegData6), .in7(RegData7), .in8(RegData8), .in9(RegData9), .in10(RegData10), .in11(RegData11),
    .in12(RegData12), .in13(RegData13), .in14(RegData14), .in15(RegData15), .in16(RegData16),
    .in17(RegData17), .in18(RegData18), .in19(RegData19), .in20(RegData20), .in21(RegData21),
    .in22(RegData22), .in23(RegData23), .in24(RegData24), .in25(RegData25), .in26(RegData26),
    .in27(RegData27), .in28(RegData28), .in29(RegData29), .in30(RegData30), .in31(RegData31), .out(RdData2),
    .sel(RdAddr2));
endmodule

module Overflow (
  input  Add,
  input  Sub,
  input  ASign,
  input  BSign,
  input  ResultSign,
  output Overflow
);

  wire and_1_out, and_2_out, or_1_out, xnor_1_out, xor_1_out, xor_2_out;

  xnor xnor_1 (xnor_1_out, ASign, BSign);
  xor xor_1 (xor_1_out, ASign, BSign);
  and and_1 (and_1_out, xnor_1_out, Add);
  and and_2 (and_2_out, xor_1_out, Sub);
  or or_1 (or_1_out, and_1_out, and_2_out);
  xor xor_2 (xor_2_out, ResultSign, ASign);
  and and_3 (Overflow, or_1_out, xor_2_out);

  // Notes on the sheet:
  //   Overflow occurs when doing addition and sign(A) == sign(B) && sign(result) != sign(A)
  //   Or
  //   Overflow occurs when doing subtraction and sign(A) != sign(B) && sign(result) != sign(A)
endmodule

module ALUCtl (
  input  [5:0] Op,
  input  [1:0] ALUOp,
  input  [5:0] Func,
  output [3:0] ALUCtl,
  output jr
);

  wire comparator_1_eq, comparator_2_eq;
  wire [3:0] aluctli_1_aluctl0, aluctlr_1_aluctl0;

  ALUCtlI aluctli_1 (
    .Op5(Op[5]), .Op4(Op[4]), .Op3(Op[3]), .Op2(Op[2]), .Op1(Op[1]), .Op0(Op[0]),
    .ALUCtl3(aluctli_1_aluctl0[3]), .ALUCtl2(aluctli_1_aluctl0[2]), .ALUCtl1(aluctli_1_aluctl0[1]),
    .ALUCtl0(aluctli_1_aluctl0[0]));
  ALUCtlR aluctlr_1 (
    .Func5(Func[5]), .Func4(Func[4]), .Func3(Func[3]), .Func2(Func[2]), .Func1(Func[1]), .Func0(Func[0]),
    .ALUCtl3(aluctlr_1_aluctl0[3]), .ALUCtl2(aluctlr_1_aluctl0[2]), .ALUCtl1(aluctlr_1_aluctl0[1]),
    .ALUCtl0(aluctlr_1_aluctl0[0]));
  Comparator #(.width(6)) comparator_1 (.a(Func), .b(6'b001000), .eq(comparator_1_eq));  // open: gt, lt
  Comparator #(.width(2)) comparator_2 (.a(ALUOp), .b(2'b10), .eq(comparator_2_eq));  // open: gt, lt
  Multiplexer #(.select(2), .width(4), .enable("false")) multiplexer_1 (
    .in0(aluctli_1_aluctl0), .in1(4'b0100), .in2(aluctlr_1_aluctl0), .out(ALUCtl), .sel(ALUOp));  // open: in3
  and and_1 (jr, comparator_1_eq, comparator_2_eq);
endmodule

module ALUCtlR (
  input  Func5,
  input  Func4,
  input  Func3,
  input  Func2,
  input  Func1,
  input  Func0,
  output ALUCtl3,
  output ALUCtl2,
  output ALUCtl1,
  output ALUCtl0
);

  wire and_2_out, and_3_out, and_4_out, and_5_out, and_6_out, and_7_out, and_8_out, and_9_out, and_10_out,
       not_1_out, not_2_out, not_3_out, not_4_out, not_5_out, not_6_out, not_7_out, not_8_out, not_9_out,
       not_10_out, not_11_out, not_12_out, not_13_out, not_14_out, not_15_out, not_16_out, not_17_out,
       not_18_out, not_19_out, not_20_out, not_21_out;

  not not_1 (not_1_out, Func5);
  not not_2 (not_2_out, Func4);
  not not_3 (not_3_out, Func3);
  not not_4 (not_4_out, Func2);
  not not_5 (not_5_out, Func0);
  not not_6 (not_6_out, Func5);
  not not_7 (not_7_out, Func4);
  not not_8 (not_8_out, Func3);
  not not_9 (not_9_out, Func0);
  not not_10 (not_10_out, Func3);
  not not_11 (not_11_out, Func0);
  not not_12 (not_12_out, Func5);
  not not_13 (not_13_out, Func4);
  not not_14 (not_14_out, Func2);
  not not_15 (not_15_out, Func0);
  not not_16 (not_16_out, Func1);
  not not_17 (not_17_out, Func0);
  not not_18 (not_18_out, Func0);
  not not_19 (not_19_out, Func2);
  not not_20 (not_20_out, Func1);
  not not_21 (not_21_out, Func2);
  and and_1 (ALUCtl3, not_1_out, not_2_out, not_3_out, not_4_out, not_5_out);
  and and_2 (and_2_out, not_6_out, not_7_out, not_8_out, not_9_out);
  and and_3 (and_3_out, not_10_out, Func1);
  and and_4 (and_4_out, Func2, not_11_out);
  and and_5 (and_5_out, not_12_out, not_13_out, not_14_out, not_15_out);
  and and_6 (and_6_out, not_16_out, not_17_out);
  and and_7 (and_7_out, Func3, not_18_out);
  and and_8 (and_8_out, not_19_out, not_20_out);
  and and_9 (and_9_out, not_21_out, Func0);
  and and_10 (and_10_out, Func2, Func1);
  or or_1 (ALUCtl2, and_2_out, and_3_out, and_4_out);
  or or_2 (ALUCtl1, and_5_out, and_6_out, and_7_out);
  or or_3 (ALUCtl0, and_8_out, and_9_out, and_10_out);
endmodule

module ALUCtlI (
  input  Op5,
  input  Op4,
  input  Op3,
  input  Op2,
  input  Op1,
  input  Op0,
  output ALUCtl3,
  output ALUCtl2,
  output ALUCtl1,
  output ALUCtl0
);

  wire and_2_out, and_3_out, and_4_out, not_1_out, not_2_out, not_3_out, not_4_out, not_5_out;

  not not_1 (not_1_out, Op0);
  not not_2 (not_2_out, Op4);
  not not_3 (not_3_out, Op2);
  not not_4 (not_4_out, Op0);
  not not_5 (not_5_out, Op0);
  not not_6 (ALUCtl0, Op2);
  and and_1 (ALUCtl2, Op2, not_1_out);
  and and_2 (and_2_out, not_2_out, not_3_out);
  and and_3 (and_3_out, Op3, not_4_out);
  and and_4 (and_4_out, Op4, not_5_out);
  or or_1 (ALUCtl1, and_2_out, and_3_out, and_4_out);

  assign ALUCtl3 = 1'b0;
endmodule

module Ctl (
  input  [5:0] Op,
  input  [5:0] Func,
  output [11:0] Signals,
  output [3:0] ALUCtl
);

  wire aluctl_1_jr, ALUOp0, ALUOp1, ALUSrcB, Branch, jal, MemRead, MemToReg, MemWrite, PCSource0, PCSource1,
       RegDst, RegWrite;

  ALUCtl aluctl_1 (.Op(Op), .Func(Func), .ALUOp({ALUOp1, ALUOp0}), .ALUCtl(ALUCtl), .jr(aluctl_1_jr));
  SubCtl0 subctl0_1 (
    .Op5(Op[5]), .Op4(Op[4]), .Op3(Op[3]), .Op2(Op[2]), .Op1(Op[1]), .Op0(Op[0]), .Branch(Branch),
    .MemRead(MemRead), .MemWrite(MemWrite), .MemToReg(MemToReg), .PCSource1(PCSource1),
    .PCSource0(PCSource0), .ALUOp1(ALUOp1), .ALUOp0(ALUOp0), .ALUSrcB(ALUSrcB), .RegWrite(RegWrite),
    .RegDst(RegDst), .jal(jal));
  Multiplexer #(.width(12), .enable("false")) multiplexer_1 (
    .in0({jal, RegDst, RegWrite, ALUSrcB, ALUOp0, ALUOp1, PCSource0, PCSource1, MemToReg, MemWrite, MemRead, Branch}),
    .in1(12'h30), .out(Signals), .sel(aluctl_1_jr));
endmodule

module IF_ID (
  input  Squash,
  input  [31:0] PCP4,
  input  [31:0] Instruction,
  input  CLK,
  output [31:0] PCP4_2,
  output [31:0] Instruction_2
);

  Register #(.width(32)) register_1 (.D(PCP4), .Q(PCP4_2), .clk(CLK), .clr(Squash));  // open: en
  Register #(.width(32)) register_2 (.D(Instruction), .Q(Instruction_2), .clk(CLK), .clr(Squash));  // open: en

  // Other names for the same wires on the sheet: S = Squash
endmodule

module ID_EX (
  input  Squash,
  input  [31:0] PCP4,
  input  [31:0] RdData1,
  input  [31:0] RdData2,
  input  [31:0] Instruction,
  input  [11:0] Signals,
  input  [3:0] ALUCtl,
  input  CLK,
  input  [4:0] WrAddr,
  output [31:0] PCP4_2,
  output [31:0] RdData1_2,
  output [31:0] RdData2_2,
  output [31:0] Instruction_2,
  output [11:0] Signals_2,
  output [3:0] ALUCtl_2,
  output [4:0] WrAddr_2
);

  Register #(.width(32)) register_1 (.D(PCP4), .Q(PCP4_2), .clk(CLK), .clr(Squash));  // open: en
  Register #(.width(32)) u_RdData1 (.D(RdData1), .Q(RdData1_2), .clk(CLK), .clr(Squash));  // open: en
  Register #(.width(32)) u_RdData2 (.D(RdData2), .Q(RdData2_2), .clk(CLK), .clr(Squash));  // open: en
  Register #(.width(32)) register_2 (.D(Instruction), .Q(Instruction_2), .clk(CLK), .clr(Squash));  // open: en
  Register #(.width(12)) u_Signals (.D(Signals), .Q(Signals_2), .clk(CLK), .clr(Squash));  // open: en
  Register #(.width(4)) u_ALUCtl (.D(ALUCtl), .Q(ALUCtl_2), .clk(CLK), .clr(Squash));  // open: en
  Register #(.width(5)) u_WrAddr (.D(WrAddr), .Q(WrAddr_2), .clk(CLK), .clr(Squash));  // open: en

  // Other names for the same wires on the sheet: S = Squash
endmodule

module EX_MEM (
  input  Squash,
  input  [31:0] PCP4,
  input  [31:0] JumpPC,
  input  [31:0] ALUOut,
  input  [31:0] WriteData,
  input  [31:0] Instruction,
  input  [31:0] RSAddr,
  input  [11:0] Signal,
  input  [3:0] ALUCtl,
  input  CLK,
  input  Zero,
  input  [4:0] WrAddr,
  output [31:0] PCP4_2,
  output [31:0] JumpPC_2,
  output [31:0] ALUOut_2,
  output [31:0] WriteData_2,
  output [31:0] Instruction_2,
  output [31:0] RSAddr_2,
  output [11:0] Signal_2,
  output [3:0] ALUCtl_2,
  output Zero_2,
  output [4:0] WrAddr_2
);

  Register #(.width(32)) register_1 (.D(PCP4), .Q(PCP4_2), .clk(CLK), .clr(Squash));  // open: en
  Register #(.width(32)) u_JumpPC (.D(JumpPC), .Q(JumpPC_2), .clk(CLK), .clr(Squash));  // open: en
  Register #(.width(32)) u_ALUOut (.D(ALUOut), .Q(ALUOut_2), .clk(CLK), .clr(Squash));  // open: en
  Register #(.width(32)) u_WriteData (.D(WriteData), .Q(WriteData_2), .clk(CLK), .clr(Squash));  // open: en
  Register #(.width(32)) register_2 (.D(Instruction), .Q(Instruction_2), .clk(CLK), .clr(Squash));  // open: en
  Register #(.width(32)) u_RSAddr (.D(RSAddr), .Q(RSAddr_2), .clk(CLK), .clr(Squash));  // open: en
  Register #(.width(12)) u_Signal (.D(Signal), .Q(Signal_2), .clk(CLK), .clr(Squash));  // open: en
  Register #(.width(4)) u_ALUCtl (.D(ALUCtl), .Q(ALUCtl_2), .clk(CLK), .clr(Squash));  // open: en
  Register #(.width(1)) u_Zero (.D(Zero), .Q(Zero_2), .clk(CLK), .clr(Squash));  // open: en
  Register #(.width(5)) u_WrAddr (.D(WrAddr), .Q(WrAddr_2), .clk(CLK), .clr(Squash));  // open: en

  // Other names for the same wires on the sheet: S = Squash
endmodule

module MEM_WB (
  input  [31:0] PC,
  input  [31:0] ReadData,
  input  [31:0] ALUOut,
  input  [31:0] Instruction,
  input  [4:0] WrAddr,
  input  [11:0] Signal,
  input  [3:0] ALUCtl,
  input  CLK,
  output [31:0] PC_2,
  output [31:0] ReadData_2,
  output [31:0] ALUOut_2,
  output [31:0] Instruction_2,
  output [4:0] WrAddr_2,
  output [11:0] Signal_2,
  output [3:0] ALUCtl_2
);

  Register #(.width(32)) u_PC (.D(PC), .Q(PC_2), .clk(CLK));  // open: en, clr
  Register #(.width(32)) u_ReadData (.D(ReadData), .Q(ReadData_2), .clk(CLK));  // open: en, clr
  Register #(.width(32)) u_ALUOut (.D(ALUOut), .Q(ALUOut_2), .clk(CLK));  // open: en, clr
  Register #(.width(32)) register_1 (.D(Instruction), .Q(Instruction_2), .clk(CLK));  // open: en, clr
  Register #(.width(5)) u_WrAddr (.D(WrAddr), .Q(WrAddr_2), .clk(CLK));  // open: en, clr
  Register #(.width(12)) u_Signal (.D(Signal), .Q(Signal_2), .clk(CLK));  // open: en, clr
  Register #(.width(4)) u_ALUCtl (.D(ALUCtl), .Q(ALUCtl_2), .clk(CLK));  // open: en, clr
endmodule

module SubCtl0 (
  input  Op5,
  input  Op4,
  input  Op3,
  input  Op2,
  input  Op1,
  input  Op0,
  output Branch,
  output MemRead,
  output MemWrite,
  output MemToReg,
  output PCSource1,
  output PCSource0,
  output ALUOp1,
  output ALUOp0,
  output ALUSrcB,
  output RegWrite,
  output RegDst,
  output jal
);

  wire and_8_out, and_9_out, and_10_out, and_11_out, and_12_out, and_13_out, and_14_out, and_15_out,
       not_1_out, not_2_out, not_3_out, not_4_out, not_5_out, not_6_out, not_7_out, not_8_out, not_9_out,
       not_10_out, not_11_out, not_12_out, not_13_out, not_14_out, not_15_out, not_16_out, not_17_out,
       not_18_out, not_19_out, not_20_out, not_21_out, not_22_out, not_23_out, not_24_out, not_25_out,
       not_26_out, not_27_out, not_28_out, not_29_out, not_30_out, not_31_out, not_32_out, not_33_out,
       not_34_out, not_35_out, not_36_out, not_37_out, not_38_out, not_39_out, not_40_out, not_41_out,
       not_42_out, not_43_out, not_44_out, not_45_out, not_46_out, not_47_out, not_48_out, not_49_out,
       not_50_out, not_51_out, not_52_out, not_53_out, not_54_out, not_55_out, not_56_out, not_57_out,
       not_58_out, not_59_out, not_60_out, not_61_out, not_62_out, not_63_out, not_64_out, not_65_out,
       not_66_out, not_67_out;

  not not_1 (not_1_out, Op5);
  not not_2 (not_2_out, Op4);
  not not_3 (not_3_out, Op3);
  not not_4 (not_4_out, Op1);
  not not_5 (not_5_out, Op0);
  not not_6 (not_6_out, Op4);
  not not_7 (not_7_out, Op3);
  not not_8 (not_8_out, Op2);
  not not_9 (not_9_out, Op4);
  not not_10 (not_10_out, Op2);
  not not_11 (not_11_out, Op4);
  not not_12 (not_12_out, Op3);
  not not_13 (not_13_out, Op2);
  not not_14 (not_14_out, Op5);
  not not_15 (not_15_out, Op4);
  not not_16 (not_16_out, Op3);
  not not_17 (not_17_out, Op2);
  not not_18 (not_18_out, Op5);
  not not_19 (not_19_out, Op4);
  not not_20 (not_20_out, Op3);
  not not_21 (not_21_out, Op1);
  not not_22 (not_22_out, Op0);
  not not_23 (not_23_out, Op5);
  not not_24 (not_24_out, Op4);
  not not_25 (not_25_out, Op3);
  not not_26 (not_26_out, Op2);
  not not_27 (not_27_out, Op1);
  not not_28 (not_28_out, Op0);
  not not_29 (not_29_out, Op5);
  not not_30 (not_30_out, Op4);
  not not_31 (not_31_out, Op3);
  not not_32 (not_32_out, Op2);
  not not_33 (not_33_out, Op5);
  not not_34 (not_34_out, Op4);
  not not_35 (not_35_out, Op3);
  not not_36 (not_36_out, Op1);
  not not_37 (not_37_out, Op0);
  not not_38 (not_38_out, Op5);
  not not_39 (not_39_out, Op4);
  not not_40 (not_40_out, Op1);
  not not_41 (not_41_out, Op0);
  not not_42 (not_42_out, Op5);
  not not_43 (not_43_out, Op4);
  not not_44 (not_44_out, Op1);
  not not_45 (not_45_out, Op4);
  not not_46 (not_46_out, Op2);
  not not_47 (not_47_out, Op5);
  not not_48 (not_48_out, Op4);
  not not_49 (not_49_out, Op2);
  not not_50 (not_50_out, Op1);
  not not_51 (not_51_out, Op0);
  not not_52 (not_52_out, Op4);
  not not_53 (not_53_out, Op3);
  not not_54 (not_54_out, Op2);
  not not_55 (not_55_out, Op5);
  not not_56 (not_56_out, Op4);
  not not_57 (not_57_out, Op1);
  not not_58 (not_58_out, Op5);
  not not_59 (not_59_out, Op4);
  not not_60 (not_60_out, Op3);
  not not_61 (not_61_out, Op2);
  not not_62 (not_62_out, Op1);
  not not_63 (not_63_out, Op0);
  not not_64 (not_64_out, Op5);
  not not_65 (not_65_out, Op4);
  not not_66 (not_66_out, Op3);
  not not_67 (not_67_out, Op2);
  and and_1 (Branch, not_1_out, not_2_out, not_3_out, Op2, not_4_out, not_5_out);
  and and_2 (MemRead, Op5, not_6_out, not_7_out, not_8_out, Op1, Op0);
  and and_3 (MemWrite, Op5, not_9_out, Op3, not_10_out, Op1, Op0);
  and and_4 (MemToReg, Op5, not_11_out, not_12_out, not_13_out, Op1, Op0);
  and and_5 (PCSource1, not_14_out, not_15_out, not_16_out, not_17_out, Op1);
  and and_6 (PCSource0, not_18_out, not_19_out, not_20_out, Op2, not_21_out, not_22_out);
  and and_7 (ALUOp1, not_23_out, not_24_out, not_25_out, not_26_out, not_27_out, not_28_out);
  and and_8 (and_8_out, not_29_out, not_30_out, not_31_out, not_32_out, Op1);
  and and_9 (and_9_out, not_33_out, not_34_out, not_35_out, Op2, not_36_out, not_37_out);
  and and_10 (and_10_out, not_38_out, not_39_out, Op3, not_40_out, not_41_out);
  and and_11 (and_11_out, not_42_out, not_43_out, Op3, Op2, not_44_out);
  and and_12 (and_12_out, Op5, not_45_out, not_46_out, Op1, Op0);
  and and_13 (and_13_out, not_47_out, not_48_out, not_49_out, not_50_out, not_51_out);
  and and_14 (and_14_out, not_52_out, not_53_out, not_54_out, Op1, Op0);
  and and_15 (and_15_out, not_55_out, not_56_out, Op3, Op2, not_57_out);
  and and_16 (RegDst, not_58_out, not_59_out, not_60_out, not_61_out, not_62_out, not_63_out);
  and and_17 (jal, not_64_out, not_65_out, not_66_out, not_67_out, Op1, Op0);
  or or_1 (ALUOp0, and_8_out, and_9_out);
  or or_2 (ALUSrcB, and_10_out, and_11_out, and_12_out);
  or or_3 (RegWrite, and_13_out, and_14_out, and_15_out);
endmodule

module Forwarding_Unit (
  input  [4:0] RAddrA,
  input  [4:0] RAddrB,
  input  [4:0] WrAddrEM,
  input  [4:0] WrAddrMW,
  input  [11:0] SignalEM,
  input  [11:0] SignalMW,
  output [1:0] FwdA,
  output [1:0] FwdB
);

  wire AEM, AMW, AZ, BEM, BMW, BZ, comparator_1_eq, comparator_4_eq, EMFA, EMFB, MWFA, MWFB, RegEMFA, RegEMFB;
  wire [1:0] multiplexer_1_out, multiplexer_2_out, multiplexer_3_out, multiplexer_5_out;

  Comparator #(.width(5)) comparator_1 (.a(RAddrA), .b({5{1'b0}}), .eq(comparator_1_eq));  // open: gt, lt
  not not_1 (AZ, comparator_1_eq);
  Comparator #(.width(5)) comparator_2 (.a(RAddrA), .b(WrAddrEM), .eq(AEM));  // open: gt, lt
  Comparator #(.width(5)) comparator_3 (.a(RAddrA), .b(WrAddrMW), .eq(AMW));  // open: gt, lt
  Comparator #(.width(5)) comparator_4 (.a(RAddrB), .b({5{1'b0}}), .eq(comparator_4_eq));  // open: gt, lt
  not not_2 (BZ, comparator_4_eq);
  Comparator #(.width(5)) comparator_5 (.a(RAddrB), .b(WrAddrEM), .eq(BEM));  // open: gt, lt
  Comparator #(.width(5)) comparator_6 (.a(RAddrB), .b(WrAddrMW), .eq(BMW));  // open: gt, lt
  and and_1 (RegEMFA, SignalEM[9], AEM, AZ, SignalEM[3]);
  and and_2 (RegEMFB, SignalEM[9], BEM, BZ, SignalEM[3]);
  Multiplexer #(.width(2), .enable("false")) multiplexer_1 (
    .in0(2'b00), .in1(2'b10), .out(multiplexer_1_out), .sel(EMFA));
  Multiplexer #(.width(2), .enable("false")) multiplexer_2 (
    .in0(2'b00), .in1(2'b10), .out(multiplexer_2_out), .sel(EMFB));
  and and_3 (EMFA, SignalEM[9], AEM, AZ);
  and and_4 (EMFB, SignalEM[9], BEM, BZ);
  Multiplexer #(.width(2), .enable("false")) multiplexer_3 (
    .in0(multiplexer_1_out), .in1(2'b01), .out(multiplexer_3_out), .sel(MWFA));
  Multiplexer #(.width(2), .enable("false")) multiplexer_4 (
    .in0(multiplexer_3_out), .in1(2'b11), .out(FwdA), .sel(RegEMFA));
  Multiplexer #(.width(2), .enable("false")) multiplexer_5 (
    .in0(multiplexer_2_out), .in1(2'b01), .out(multiplexer_5_out), .sel(MWFB));
  Multiplexer #(.width(2), .enable("false")) multiplexer_6 (
    .in0(multiplexer_5_out), .in1(2'b11), .out(FwdB), .sel(RegEMFB));
  and and_5 (MWFA, SignalMW[9], AMW, AZ, ~EMFA);  // AND_Gate
  and and_6 (MWFB, SignalMW[9], BMW, BZ, ~EMFB);  // AND_Gate

  // Other names for the same wires on the sheet: MemToRegEM = SignalEM[3]; RegWriteEM = SignalEM[9];
  //   RegWriteMW = SignalMW[9]
endmodule

module Register_Forwarding_Unit (
  input  [4:0] RAddrA,
  input  [4:0] RAddrB,
  input  [4:0] WrAddr,
  input  RegWrite,
  output FwdA,
  output FwdB
);

  wire A, AZ, B, BZ, comparator_1_eq, comparator_3_eq, FA, FB;

  not not_1 (AZ, comparator_1_eq);
  Comparator #(.width(5)) comparator_1 (.a(RAddrA), .b({5{1'b0}}), .eq(comparator_1_eq));  // open: gt, lt
  Comparator #(.width(5)) comparator_2 (.a(RAddrA), .b(WrAddr), .eq(A));  // open: gt, lt
  Comparator #(.width(5)) comparator_3 (.a(RAddrB), .b({5{1'b0}}), .eq(comparator_3_eq));  // open: gt, lt
  not not_2 (BZ, comparator_3_eq);
  Comparator #(.width(5)) comparator_4 (.a(RAddrB), .b(WrAddr), .eq(B));  // open: gt, lt
  Multiplexer #(.enable("false")) multiplexer_1 (.in0(1'b0), .in1(1'b1), .out(FwdA), .sel(FA));
  Multiplexer #(.enable("false")) multiplexer_2 (.in0(1'b0), .in1(1'b1), .out(FwdB), .sel(FB));
  and and_1 (FA, RegWrite, A, AZ);
  and and_2 (FB, RegWrite, B, BZ);
endmodule

module JR_Forwarding_Unit (
  input  JR,
  input  [4:0] WrAddr,
  input  [4:0] RAddrJR,
  input  RegWrite,
  output FwdJR
);

  wire A, AZ, comparator_1_eq, FA;

  Comparator #(.width(5)) comparator_1 (.a(RAddrJR), .b({5{1'b0}}), .eq(comparator_1_eq));  // open: gt, lt
  not not_1 (AZ, comparator_1_eq);
  Comparator #(.width(5)) comparator_2 (.a(RAddrJR), .b(WrAddr), .eq(A));  // open: gt, lt
  and and_1 (FA, JR, A, RegWrite, AZ);
  Multiplexer #(.enable("false")) multiplexer_1 (.in0(1'b0), .in1(1'b1), .out(FwdJR), .sel(FA));
endmodule
